// Logisim project control_logic.circ as structural Verilog: 13 circuits, main circuit control_logic
module control_logic (
  input  [31:0] inst,
  input  BrEq,
  input  BrLt,
  output PCSel,
  output RegWEn,
  output [2:0] ImmSel,
  output BrUn,
  output ASel,
  output BSel,
  output [3:0] ALUSel,
  output MemRW,
  output [1:0] WBSel
);

  makePCSel makepcsel_1 (.instr(inst), .BrEq(BrEq), .BrLt(BrLt), .PCSel(PCSel));
  makeRegWEn makeregwen_1 (.instr(inst), .RegWEn(RegWEn));
  makeImmSel makeimmsel_1 (.instr(inst), .ImmSel(ImmSel));
  makeBrUn makebrun_1 (.in_1(inst), .BrUn(BrUn));
  makeASel makeasel_1 (.instr(inst), .ASel(ASel));
  makeBSel makebsel_1 (.instr(inst), .BSel(BSel));
  makeALUSel makealusel_1 (.in_1(inst), .out_2(ALUSel));
  makeMemRW makememrw_1 (.in_1(inst), .out_2(MemRW));
  makeWBSel makewbsel_1 (.instr(inst), .WBSel(WBSel));

  // Notes on the sheet:
  //   INPUTS to your circuit
  //   DON'T CHANGE THE LOCATIONS OF THE INPUTS AND OUTPUTS!
  //   OUTPUT from your circuit
endmodule

module makeImmSel (
  input  [31:0] instr,
  output [2:0] ImmSel
);

  wire comparator_1_eq, comparator_2_eq, comparator_3_eq, comparator_4_eq, comparator_5_eq, comparator_6_eq,
       comparator_7_eq, comparator_8_eq, or_1_out, or_2_out;
  wire [6:0] opcode;

  Comparator #(.width(7)) comparator_1 (.a(opcode), .b(7'b0000011), .eq(comparator_1_eq));  // open: gt, lt
  Comparator #(.width(7)) comparator_2 (.a(opcode), .b(7'b1100111), .eq(comparator_2_eq));  // open: gt, lt
  Comparator #(.width(7)) comparator_3 (.a(opcode), .b(7'b0010011), .eq(comparator_3_eq));  // open: gt, lt
  Comparator #(.width(7)) comparator_4 (.a(opcode), .b(7'b0100011), .eq(comparator_4_eq));  // open: gt, lt
  Comparator #(.width(7)) comparator_5 (.a(opcode), .b(7'b1100011), .eq(comparator_5_eq));  // open: gt, lt
  Comparator #(.width(7)) comparator_6 (.a(opcode), .b(7'b0010111), .eq(comparator_6_eq));  // open: gt, lt
  Comparator #(.width(7)) comparator_7 (.a(opcode), .b(7'b0110111), .eq(comparator_7_eq));  // open: gt, lt
  Comparator #(.width(7)) comparator_8 (.a(opcode), .b(7'b1101111), .eq(comparator_8_eq));  // open: gt, lt
  or or_1 (or_1_out, comparator_1_eq, comparator_2_eq, comparator_3_eq);
  or or_2 (or_2_out, comparator_6_eq, comparator_7_eq);
  assign ImmSel = or_1_out ? 3'b000 : 3'bz;  // Controlled_Buffer I_type
  assign ImmSel = comparator_4_eq ? 3'b001 : 3'bz;  // Controlled_Buffer S
  assign ImmSel = comparator_5_eq ? 3'b010 : 3'bz;  // Controlled_Buffer SB
  assign ImmSel = or_2_out ? 3'b011 : 3'bz;  // Controlled_Buffer U_type
  assign ImmSel = comparator_8_eq ? 3'b100 : 3'bz;  // Controlled_Buffer UJ
  getOP getop_1 (.instr(instr), .opcode(opcode));

  // Other names for the same wires on the sheet: inst[31:0] = instr

  // Notes on the sheet:
  //   complete
endmodule

module getOP (
  input  [31:0] instr,
  output [6:0] opcode
);


  assign opcode = instr[6:0];
endmodule

module makeASel (
  input  [31:0] instr,
  output ASel
);

  wire comparator_1_eq, comparator_2_eq, comparator_3_eq, comparator_4_eq, comparator_5_eq, or_1_out;
  wire [6:0] opcode;

  Comparator #(.width(7)) comparator_1 (.a(opcode), .b(7'b0110011), .eq(comparator_1_eq));  // open: gt, lt
  Comparator #(.width(7)) comparator_2 (.a(opcode), .b(7'b0000011), .eq(comparator_2_eq));  // open: gt, lt
  Comparator #(.width(7)) comparator_3 (.a(opcode), .b(7'b0010011), .eq(comparator_3_eq));  // open: gt, lt
  Comparator #(.width(7)) comparator_4 (.a(opcode), .b(7'b0100011), .eq(comparator_4_eq));  // open: gt, lt
  Comparator #(.width(7)) comparator_5 (.a(opcode), .b(7'b1100111), .eq(comparator_5_eq));  // open: gt, lt
  getOP getop_1 (.instr(instr), .opcode(opcode));
  not not_1 (ASel, or_1_out);
  or or_1 (or_1_out, comparator_1_eq, comparator_2_eq, comparator_3_eq, comparator_4_eq, comparator_5_eq);

  // Other names for the same wires on the sheet: inst[31:0] = instr

  // Notes on the sheet:
  //   done
  //   all these instr need to use rs1 for A
endmodule

module makeBSel (
  input  [31:0] instr,
  output BSel
);

  wire comparator_1_eq, comparator_2_eq, comparator_3_eq, comparator_4_eq, comparator_5_eq, comparator_6_eq,
       comparator_7_eq, comparator_8_eq;
  wire [6:0] opcode;

  Comparator #(.width(7)) comparator_1 (.a(opcode), .b(7'b0000011), .eq(comparator_1_eq));  // open: gt, lt
  Comparator #(.width(7)) comparator_2 (.a(opcode), .b(7'b0010011), .eq(comparator_2_eq));  // open: gt, lt
  Comparator #(.width(7)) comparator_3 (.a(opcode), .b(7'b0100011), .eq(comparator_3_eq));  // open: gt, lt
  Comparator #(.width(7)) comparator_4 (.a(opcode), .b(7'b1100011), .eq(comparator_4_eq));  // open: gt, lt
  Comparator #(.width(7)) comparator_5 (.a(opcode), .b(7'b0010111), .eq(comparator_5_eq));  // open: gt, lt
  Comparator #(.width(7)) comparator_6 (.a(opcode), .b(7'b0110111), .eq(comparator_6_eq));  // open: gt, lt
  Comparator #(.width(7)) comparator_7 (.a(opcode), .b(7'b1101111), .eq(comparator_7_eq));  // open: gt, lt
  Comparator #(.width(7)) comparator_8 (.a(opcode), .b(7'b1100111), .eq(comparator_8_eq));  // open: gt, lt
  or or_1 (BSel, comparator_1_eq, comparator_2_eq, comparator_3_eq, comparator_4_eq, comparator_5_eq, comparator_6_eq, comparator_7_eq, comparator_8_eq);
  getOP getop_1 (.instr(instr), .opcode(opcode));

  // Other names for the same wires on the sheet: inst[31:0] = instr

  // Notes on the sheet:
  //   done
endmodule

module makeALUSel (
  input  [31:0] in_1,
  output [3:0] out_2
);

  wire and_1_out, and_2_out, and_3_out, and_4_out, and_5_out, and_6_out, and_7_out, and_8_out, and_9_out,
       and_10_out, and_11_out, and_12_out, and_13_out, and_14_out, and_15_out, and_16_out, and_17_out,
       comparator_9_eq, comparator_10_eq, comparator_11_eq, comparator_12_eq, comparator_13_eq,
       comparator_14_eq, comparator_15_eq, comparator_16_eq, comparator_17_eq, comparator_18_eq,
       comparator_19_eq, comparator_20_eq, comparator_21_eq, comparator_22_eq, comparator_23_eq,
       comparator_24_eq, comparator_25_eq, comparator_26_eq, comparator_27_eq, comparator_28_eq,
       comparator_29_eq, comparator_30_eq, comparator_31_eq, comparator_32_eq, comparator_33_eq,
       comparator_34_eq, comparator_35_eq, comparator_36_eq, comparator_37_eq, comparator_38_eq,
       comparator_39_eq, comparator_40_eq, comparator_41_eq, comparator_42_eq, comparator_43_eq,
       comparator_44_eq, comparator_45_eq, comparator_46_eq, comparator_47_eq, comparator_48_eq,
       comparator_49_eq, comparator_50_eq, comparator_51_eq, comparator_52_eq, IInstrResEn1, IInstrResEn2,
       jalResEn, RInstrResEn, SBInstrResEn, SInstrResEn, UJInstrResEn, UResEn;
  wire [2:0] func3;
  wire [3:0] IInstrRes1, IInstrRes2, RInstrRes, SInstrRes;
  wire [6:0] func7, opcode;

  Comparator #(.width(7)) comparator_1 (.a(opcode), .b(7'b0110011), .eq(RInstrResEn));  // open: gt, lt
  Comparator #(.width(7)) comparator_2 (.a(opcode), .b(7'b0000011), .eq(IInstrResEn1));  // open: gt, lt
  Comparator #(.width(7)) comparator_3 (.a(opcode), .b(7'b0010011), .eq(IInstrResEn2));  // open: gt, lt
  Comparator #(.width(7)) comparator_4 (.a(opcode), .b(7'b0100011), .eq(SInstrResEn));  // open: gt, lt
  Comparator #(.width(7)) comparator_5 (.a(opcode), .b(7'b1100011), .eq(SBInstrResEn));  // open: gt, lt
  Comparator #(.width(7)) comparator_6 (.a(opcode), .b(7'b0010111), .eq(UResEn));  // open: gt, lt
  Comparator #(.width(7)) comparator_7 (.a(opcode), .b(7'b1101111), .eq(UJInstrResEn));  // open: gt, lt
  Comparator #(.width(7)) comparator_8 (.a(opcode), .b(7'b1100111), .eq(jalResEn));  // open: gt, lt
  assign out_2 = RInstrResEn ? RInstrRes : 4'bz;  // Controlled_Buffer controlled_buffer_1
  assign out_2 = IInstrResEn1 ? IInstrRes1 : 4'bz;  // Controlled_Buffer controlled_buffer_2
  assign out_2 = IInstrResEn2 ? IInstrRes2 : 4'bz;  // Controlled_Buffer controlled_buffer_3
  assign out_2 = SInstrResEn ? SInstrRes : 4'bz;  // Controlled_Buffer controlled_buffer_4
  assign out_2 = SBInstrResEn ? 4'b0000 : 4'bz;  // Controlled_Buffer controlled_buffer_5
  assign out_2 = UResEn ? 4'b0000 : 4'bz;  // Controlled_Buffer controlled_buffer_6
  assign out_2 = UJInstrResEn ? 4'b0000 : 4'bz;  // Controlled_Buffer controlled_buffer_7
  assign out_2 = jalResEn ? 4'b0000 : 4'bz;  // Controlled_Buffer controlled_buffer_8
  getFunc7 getfunc7_1 (.instr(in_1), .func7(func7));
  getFunc3 getfunc3_1 (.instr(in_1), .func3(func3));
  getOP getop_1 (.instr(in_1), .opcode(opcode));
  Comparator #(.width(3)) comparator_9 (.a(func3), .b(3'b000), .eq(comparator_9_eq));  // open: gt, lt
  and and_1 (and_1_out, comparator_9_eq, comparator_10_eq);
  Comparator #(.width(7)) comparator_10 (.a(func7), .b({7{1'b0}}), .eq(comparator_10_eq));  // open: gt, lt
  Comparator #(.width(3)) comparator_11 (.a(func3), .b(3'b000), .eq(comparator_11_eq));  // open: gt, lt
  and and_2 (and_2_out, comparator_11_eq, comparator_12_eq);
  Comparator #(.width(7)) comparator_12 (.a(func7), .b(7'b0000001), .eq(comparator_12_eq));  // open: gt, lt
  Comparator #(.width(3)) comparator_13 (.a(func3), .b(3'b000), .eq(comparator_13_eq));  // open: gt, lt
  and and_3 (and_3_out, comparator_13_eq, comparator_14_eq);
  Comparator #(.width(7)) comparator_14 (.a(func7), .b(7'b0100000), .eq(comparator_14_eq));  // open: gt, lt
  Comparator #(.width(3)) comparator_15 (.a(func3), .b(3'b001), .eq(comparator_15_eq));  // open: gt, lt
  and and_4 (and_4_out, comparator_15_eq, comparator_16_eq);
  Comparator #(.width(7)) comparator_16 (.a(func7), .b({7{1'b0}}), .eq(comparator_16_eq));  // open: gt, lt
  Comparator #(.width(3)) comparator_17 (.a(func3), .b(3'b001), .eq(comparator_17_eq));  // open: gt, lt
  and and_5 (and_5_out, comparator_17_eq, comparator_18_eq);
  Comparator #(.width(7)) comparator_18 (.a(func7), .b(7'b0000001), .eq(comparator_18_eq));  // open: gt, lt
  Comparator #(.width(3)) comparator_19 (.a(func3), .b(3'b011), .eq(comparator_19_eq));  // open: gt, lt
  and and_6 (and_6_out, comparator_19_eq, comparator_20_eq);
  Comparator #(.width(7)) comparator_20 (.a(func7), .b(7'b0000001), .eq(comparator_20_eq));  // open: gt, lt
  Comparator #(.width(3)) comparator_21 (.a(func3), .b(3'b010), .eq(comparator_21_eq));  // open: gt, lt
  and and_7 (and_7_out, comparator_21_eq, comparator_22_eq);
  Comparator #(.width(7)) comparator_22 (.a(func7), .b({7{1'b0}}), .eq(comparator_22_eq));  // open: gt, lt
  Comparator #(.width(3)) comparator_23 (.a(func3), .b(3'b100), .eq(comparator_23_eq));  // open: gt, lt
  and and_8 (and_8_out, comparator_23_eq, comparator_24_eq);
  Comparator #(.width(7)) comparator_24 (.a(func7), .b({7{1'b0}}), .eq(comparator_24_eq));  // open: gt, lt
  Comparator #(.width(3)) comparator_25 (.a(func3), .b(3'b101), .eq(comparator_25_eq));  // open: gt, lt
  and and_9 (and_9_out, comparator_25_eq, comparator_26_eq);
  Comparator #(.width(7)) comparator_26 (.a(func7), .b(7'b0000001), .eq(comparator_26_eq));  // open: gt, lt
  Comparator #(.width(3)) comparator_27 (.a(func3), .b(3'b101), .eq(comparator_27_eq));  // open: gt, lt
  and and_10 (and_10_out, comparator_27_eq, comparator_28_eq);
  Comparator #(.width(7)) comparator_28 (.a(func7), .b({7{1'b0}}), .eq(comparator_28_eq));  // open: gt, lt
  Comparator #(.width(3)) comparator_29 (.a(func3), .b(3'b101), .eq(comparator_29_eq));  // open: gt, lt
  and and_11 (and_11_out, comparator_29_eq, comparator_30_eq);
  Comparator #(.width(7)) comparator_30 (.a(func7), .b(7'b0100000), .eq(comparator_30_eq));  // open: gt, lt
  Comparator #(.width(3)) comparator_31 (.a(func3), .b(3'b110), .eq(comparator_31_eq));  // open: gt, lt
  and and_12 (and_12_out, comparator_31_eq, comparator_32_eq);
  Comparator #(.width(7)) comparator_32 (.a(func7), .b({7{1'b0}}), .eq(comparator_32_eq));  // open: gt, lt
  Comparator #(.width(3)) comparator_33 (.a(func3), .b(3'b111), .eq(comparator_33_eq));  // open: gt, lt
  and and_13 (and_13_out, comparator_33_eq, comparator_34_eq);
  Comparator #(.width(7)) comparator_34 (.a(func7), .b(7'b0000001), .eq(comparator_34_eq));  // open: gt, lt
  Comparator #(.width(3)) comparator_35 (.a(func3), .b(3'b111), .eq(comparator_35_eq));  // open: gt, lt
  and and_14 (and_14_out, comparator_35_eq, comparator_36_eq);
  Comparator #(.width(7)) comparator_36 (.a(func7), .b({7{1'b0}}), .eq(comparator_36_eq));  // open: gt, lt
  assign RInstrRes = and_1_out ? 4'b0000 : 4'bz;  // Controlled_Buffer add
  assign RInstrRes = and_2_out ? 4'b1010 : 4'bz;  // Controlled_Buffer myMul
  assign RInstrRes = and_3_out ? 4'b1100 : 4'bz;  // Controlled_Buffer mySub
  assign RInstrRes = and_4_out ? 4'b0110 : 4'bz;  // Controlled_Buffer mySll
  assign RInstrRes = and_5_out ? 4'b1110 : 4'bz;  // Controlled_Buffer mulh
  assign RInstrRes = and_6_out ? 4'b1011 : 4'bz;  // Controlled_Buffer myMulhu
  assign RInstrRes = and_7_out ? 4'b0111 : 4'bz;  // Controlled_Buffer mySlt
  assign RInstrRes = and_8_out ? 4'b0011 : 4'bz;  // Controlled_Buffer myXor
  assign RInstrRes = and_9_out ? 4'b1000 : 4'bz;  // Controlled_Buffer myDivu
  assign RInstrRes = and_10_out ? 4'b0100 : 4'bz;  // Controlled_Buffer mySrl
  assign RInstrRes = and_11_out ? 4'b0101 : 4'bz;  // Controlled_Buffer mySra
  assign RInstrRes = and_12_out ? 4'b0010 : 4'bz;  // Controlled_Buffer myOr
  assign RInstrRes = and_13_out ? 4'b1001 : 4'bz;  // Controlled_Buffer myRemu
  assign RInstrRes = and_14_out ? 4'b0001 : 4'bz;  // Controlled_Buffer myAnd
  Comparator #(.width(3)) comparator_37 (.a(func3), .b(3'b000), .eq(comparator_37_eq));  // open: gt, lt
  Comparator #(.width(3)) comparator_38 (.a(func3), .b(3'b001), .eq(comparator_38_eq));  // open: gt, lt
  Comparator #(.width(3)) comparator_39 (.a(func3), .b(3'b010), .eq(comparator_39_eq));  // open: gt, lt
  assign IInstrRes1 = comparator_37_eq ? 4'b0000 : 4'bz;  // Controlled_Buffer lb
  assign IInstrRes1 = comparator_38_eq ? 4'b0000 : 4'bz;  // Controlled_Buffer lh
  assign IInstrRes1 = comparator_39_eq ? 4'b0000 : 4'bz;  // Controlled_Buffer lw
  Comparator #(.width(3)) comparator_40 (.a(func3), .b(3'b000), .eq(comparator_40_eq));  // open: gt, lt
  Comparator #(.width(3)) comparator_41 (.a(func3), .b(3'b001), .eq(comparator_41_eq));  // open: gt, lt
  and and_15 (and_15_out, comparator_41_eq, comparator_42_eq);
  Comparator #(.width(7)) comparator_42 (.a(func7), .b({7{1'b0}}), .eq(comparator_42_eq));  // open: gt, lt
  Comparator #(.width(3)) comparator_43 (.a(func3), .b(3'b010), .eq(comparator_43_eq));  // open: gt, lt
  Comparator #(.width(3)) comparator_44 (.a(func3), .b(3'b100), .eq(comparator_44_eq));  // open: gt, lt
  Comparator #(.width(3)) comparator_45 (.a(func3), .b(3'b101), .eq(comparator_45_eq));  // open: gt, lt
  Comparator #(.width(7)) comparator_46 (.a(func7), .b({7{1'b0}}), .eq(comparator_46_eq));  // open: gt, lt
  Comparator #(.width(3)) comparator_47 (.a(func3), .b(3'b101), .eq(comparator_47_eq));  // open: gt, lt
  Comparator #(.width(7)) comparator_48 (.a(func7), .b(7'b0100000), .eq(comparator_48_eq));  // open: gt, lt
  Comparator #(.width(3)) comparator_49 (.a(func3), .b(3'b110), .eq(comparator_49_eq));  // open: gt, lt
  Comparator #(.width(3)) comparator_50 (.a(func3), .b(3'b111), .eq(comparator_50_eq));  // open: gt, lt
  assign IInstrRes2 = comparator_40_eq ? 4'b0000 : 4'bz;  // Controlled_Buffer addi
  assign IInstrRes2 = and_15_out ? 4'b0110 : 4'bz;  // Controlled_Buffer slli
  assign IInstrRes2 = comparator_43_eq ? 4'b0111 : 4'bz;  // Controlled_Buffer slti
  assign IInstrRes2 = comparator_44_eq ? 4'b0011 : 4'bz;  // Controlled_Buffer xori
  and and_16 (and_16_out, comparator_45_eq, comparator_46_eq);
  assign IInstrRes2 = and_16_out ? 4'b0100 : 4'bz;  // Controlled_Buffer srli
  and and_17 (and_17_out, comparator_47_eq, comparator_48_eq);
  assign IInstrRes2 = and_17_out ? 4'b0101 : 4'bz;  // Controlled_Buffer srai
  assign IInstrRes2 = comparator_49_eq ? 4'b0010 : 4'bz;  // Controlled_Buffer ori
  assign IInstrRes2 = comparator_50_eq ? 4'b0001 : 4'bz;  // Controlled_Buffer andi
  Comparator #(.width(3)) comparator_51 (.a(func3), .b(3'b010), .eq(comparator_51_eq));  // open: gt, lt
  Comparator #(.width(3)) comparator_52 (.a(func3), .b(3'b111), .eq(comparator_52_eq));  // open: gt, lt
  assign SInstrRes = comparator_51_eq ? 4'b1101 : 4'bz;  // Controlled_Buffer sw
  assign SInstrRes = comparator_52_eq ? 4'b0000 : 4'bz;  // Controlled_Buffer swlt

  // Other names for the same wires on the sheet: ALUSel[3:0] = out_2; inst[31:0] = in_1

  // Notes on the sheet:
  //   R type instructions
  //   I
  //   i
endmodule

module getFunc3 (
  input  [31:0] instr,
  output [2:0] func3
);


  assign func3 = instr[14:12];
endmodule

module getFunc7 (
  input  [31:0] instr,
  output [6:0] func7
);


  assign func7 = instr[31:25];
endmodule

module makeRegWEn (
  input  [31:0] instr,
  output RegWEn
);

  wire comparator_1_eq, comparator_2_eq, comparator_3_eq, comparator_4_eq, comparator_5_eq, comparator_6_eq,
       comparator_7_eq;
  wire [6:0] opcode;

  Comparator #(.width(7)) comparator_1 (.a(opcode), .b(7'b0110011), .eq(comparator_1_eq));  // open: gt, lt
  Comparator #(.width(7)) comparator_2 (.a(opcode), .b(7'b0000011), .eq(comparator_2_eq));  // open: gt, lt
  Comparator #(.width(7)) comparator_3 (.a(opcode), .b(7'b0010011), .eq(comparator_3_eq));  // open: gt, lt
  Comparator #(.width(7)) comparator_4 (.a(opcode), .b(7'b1100111), .eq(comparator_4_eq));  // open: gt, lt
  Comparator #(.width(7)) comparator_5 (.a(opcode), .b(7'b0010111), .eq(comparator_5_eq));  // open: gt, lt
  Comparator #(.width(7)) comparator_6 (.a(opcode), .b(7'b0110111), .eq(comparator_6_eq));  // open: gt, lt
  Comparator #(.width(7)) comparator_7 (.a(opcode), .b(7'b1101111), .eq(comparator_7_eq));  // open: gt, lt
  or or_1 (RegWEn, comparator_1_eq, comparator_2_eq, comparator_3_eq, comparator_4_eq, comparator_5_eq, comparator_6_eq, comparator_7_eq);
  getOP getop_1 (.instr(instr), .opcode(opcode));

  // Other names for the same wires on the sheet: inst[31:0] = instr

  // Notes on the sheet:
  //   r
  //   I1
  //   I2
  //   I3(jalr)
  //   U1
  //   U2
  //   UJ
  //   done
endmodule

module makeWBSel (
  input  [31:0] instr,
  output [1:0] WBSel
);

  wire chooseAlu, chooseImm, chooseMem, choosePCp4, comparator_1_eq, comparator_2_eq, comparator_3_eq,
       comparator_4_eq, comparator_5_eq, comparator_6_eq, comparator_7_eq, comparator_8_eq;
  wire [6:0] opcode;

  Comparator #(.width(7)) comparator_1 (.a(opcode), .b(7'b0000011), .eq(comparator_1_eq));  // open: gt, lt
  Comparator #(.width(7)) comparator_2 (.a(opcode), .b(7'b0100011), .eq(comparator_2_eq));  // open: gt, lt
  or or_1 (chooseMem, comparator_1_eq, comparator_2_eq);
  assign WBSel = chooseMem ? 2'b00 : 2'bz;  // Controlled_Buffer controlled_buffer_1
  assign WBSel = chooseAlu ? 2'b01 : 2'bz;  // Controlled_Buffer controlled_buffer_2
  assign WBSel = choosePCp4 ? 2'b10 : 2'bz;  // Controlled_Buffer controlled_buffer_3
  assign WBSel = chooseImm ? 2'b11 : 2'bz;  // Controlled_Buffer controlled_buffer_4
  // Probe on opcode
  getOP getop_1 (.instr(instr), .opcode(opcode));
  Comparator #(.width(7)) comparator_3 (.a(opcode), .b(7'b0110011), .eq(comparator_3_eq));  // open: gt, lt
  Comparator #(.width(7)) comparator_4 (.a(opcode), .b(7'b0010011), .eq(comparator_4_eq));  // open: gt, lt
  Comparator #(.width(7)) comparator_5 (.a(opcode), .b(7'b1100011), .eq(comparator_5_eq));  // open: gt, lt
  Comparator #(.width(7)) comparator_6 (.a(opcode), .b(7'b0010111), .eq(comparator_6_eq));  // open: gt, lt
  // Probe on chooseAlu
  or or_2 (chooseAlu, comparator_3_eq, comparator_4_eq, comparator_5_eq, comparator_6_eq);
  // Probe on opcode
  Comparator #(.width(7)) comparator_7 (.a(opcode), .b(7'b1100111), .eq(comparator_7_eq));  // open: gt, lt
  Comparator #(.width(7)) comparator_8 (.a(opcode), .b(7'b1101111), .eq(comparator_8_eq));  // open: gt, lt
  or or_3 (choosePCp4, comparator_7_eq, comparator_8_eq);
  Comparator #(.width(7)) comparator_9 (.a(opcode), .b(7'b0110111), .eq(chooseImm));  // open: gt, lt

  // Other names for the same wires on the sheet: inst[31:0] = instr

  // Notes on the sheet:
  //   generally done
endmodule

module makePCSel (
  input  [31:0] instr,
  input  BrEq,
  input  BrLt,
  output PCSel
);

  wire beq, beqEn, bgeEn, bgeuEn, bltEn, bltuEn, bneEn, comparator_7_eq, jalNeedBranch, jalrNeedBranch,
       not_1_out, not_2_out, or_1_out, or_2_out, SBNeedBranch;
  wire [2:0] func3;
  wire [6:0] opcode;

  Comparator #(.width(3)) comparator_1 (.a(func3), .b(3'b000), .eq(beqEn));  // open: gt, lt
  Comparator #(.width(3)) comparator_2 (.a(func3), .b(3'b001), .eq(bneEn));  // open: gt, lt
  Comparator #(.width(3)) comparator_3 (.a(func3), .b(3'b100), .eq(bltEn));  // open: gt, lt
  Comparator #(.width(3)) comparator_4 (.a(func3), .b(3'b101), .eq(bgeEn));  // open: gt, lt
  Comparator #(.width(3)) comparator_5 (.a(func3), .b(3'b110), .eq(bltuEn));  // open: gt, lt
  Comparator #(.width(3)) comparator_6 (.a(func3), .b(3'b111), .eq(bgeuEn));  // open: gt, lt
  Comparator #(.width(7)) comparator_7 (.a(opcode), .b(7'b1100011), .eq(comparator_7_eq));  // open: gt, lt
  Comparator #(.width(7)) comparator_8 (.a(opcode), .b(7'b1101111), .eq(jalNeedBranch));  // open: gt, lt
  Comparator #(.width(7)) comparator_9 (.a(opcode), .b(7'b1100111), .eq(jalrNeedBranch));  // open: gt, lt
  and and_1 (SBNeedBranch, beq, comparator_7_eq);
  getOP getop_1 (.instr(instr), .opcode(opcode));
  getFunc3 getfunc3_1 (.instr(instr), .func3(func3));
  not not_1 (not_1_out, BrEq);
  not not_2 (not_2_out, BrLt);
  // Probe on beqEn
  assign beq = beqEn ? BrEq : 1'bz;  // Controlled_Buffer controlled_buffer_1
  assign beq = bneEn ? not_1_out : 1'bz;  // Controlled_Buffer controlled_buffer_2
  or or_1 (or_1_out, bltuEn, bltEn);
  assign beq = or_1_out ? BrLt : 1'bz;  // Controlled_Buffer controlled_buffer_3
  or or_2 (or_2_out, bgeuEn, bgeEn);
  assign beq = or_2_out ? not_2_out : 1'bz;  // Controlled_Buffer controlled_buffer_4
  or or_3 (PCSel, SBNeedBranch, jalNeedBranch, jalrNeedBranch);

  // Other names for the same wires on the sheet: bge = beq; blt = beq; bne = beq; inst[31:0] = instr

  // Notes on the sheet:
  //   completed
  //   for SB
endmodule

module makeBrUn (
  input  [31:0] in_1,
  output BrUn
);

  wire comparator_1_eq, comparator_2_eq, comparator_3_eq, or_1_out;
  wire [2:0] func3;
  wire [6:0] opcode;

  Comparator #(.width(7)) comparator_1 (.a(opcode), .b(7'b1100011), .eq(comparator_1_eq));  // open: gt, lt
  Comparator #(.width(3)) comparator_2 (.a(func3), .b(3'b110), .eq(comparator_2_eq));  // open: gt, lt
  Comparator #(.width(3)) comparator_3 (.a(func3), .b(3'b111), .eq(comparator_3_eq));  // open: gt, lt
  getOP getop_1 (.instr(in_1), .opcode(opcode));
  getFunc3 getfunc3_1 (.instr(in_1), .func3(func3));
  or or_1 (or_1_out, comparator_2_eq, comparator_3_eq);
  and and_1 (BrUn, comparator_1_eq, or_1_out);

  // Other names for the same wires on the sheet: inst[31:0] = in_1
endmodule

module makeMemRW (
  input  [31:0] in_1,
  output out_2
);

  wire MemReadEn;
  wire [6:0] opcode;

  Comparator #(.width(7)) comparator_1 (.a(opcode), .b(7'b0010011), .eq(MemReadEn));  // open: gt, lt
  Comparator #(.width(7)) comparator_2 (.a(opcode), .b(7'b0100011), .eq(out_2));  // open: gt, lt
  getOP getop_1 (.instr(in_1), .opcode(opcode));

  // Other names for the same wires on the sheet: inst[31:0] = in_1; MemRW = out_2; MemWriteEn = out_2

  // Notes on the sheet:
  //   only enable writing when sw, other times, read mem (as we don't have a third option)
endmodule
