// Logisim project cpu.circ as structural Verilog: 5 circuits, main circuit main
module main (
  input  [31:0] INSTRUCTION,
  input  CLOCK,
  output [31:0] PROGRAM_COUNTER,
  output [31:0] ra,
  output [31:0] sp,
  output [31:0] t0,
  output [31:0] t1,
  output [31:0] t2,
  output [31:0] s0,
  output [31:0] s1,
  output [31:0] a0
);

  wire ASel, BrEq, BrLt, BrUn, BSel, DMEM_p6, MemRW, PCSel, RegWEn;
  wire [1:0] WBSel;
  wire [2:0] ImmSel;
  wire [3:0] ALUSel;
  wire [4:0] rd, rs1, rs2;
  wire [31:0] A, adder_1_out, ALURes, B, Imm, INSTRUCTION_Next, MemData, multiplexer_1_out,
       multiplexer_2_out, PCplus4, PROGRAM_COUNTER_Next, rs1val, rs2val, WBdata;

  Adder #(.width(32)) adder_1 (.a(PROGRAM_COUNTER), .b(32'h4), .out(adder_1_out));  // open: cin, cout
  Multiplexer #(.width(32), .enable("false")) multiplexer_1 (
    .in0(adder_1_out), .in1(ALURes), .out(multiplexer_1_out), .sel(PCSel));
  Register #(.width(32)) PC (.D(multiplexer_1_out), .clk(CLOCK), .Q(PROGRAM_COUNTER));  // open: en, clr
  Multiplexer #(.width(32), .enable("false")) multiplexer_2 (
    .in0(INSTRUCTION), .in1(32'h13), .out(multiplexer_2_out), .sel(PCSel));
  control_logic control_logic_1 (
    .BSel(BSel), .ASel(ASel), .BrUn(BrUn), .ImmSel(ImmSel), .RegWEn(RegWEn), .PCSel(PCSel), .BrLt(BrLt),
    .BrEq(BrEq), .inst(INSTRUCTION_Next), .ALUSel(ALUSel), .MemRW(MemRW), .WBSel(WBSel));
  Register #(.width(32)) IR (.D(multiplexer_2_out), .clk(CLOCK), .Q(INSTRUCTION_Next));  // open: en, clr
  Register #(.width(32)) register_1 (.D(PROGRAM_COUNTER), .clk(CLOCK), .Q(PROGRAM_COUNTER_Next));  // open: en, clr
  // Probe on nothing
  // Probe on rs1
  // Probe on rs2
  // Probe on rd
  // Probe on WBdata
  // Probe on INSTRUCTION_Next
  // Probe on RegWEn
  // Probe on ImmSel
  // Probe on INSTRUCTION_Next
  getRs getrs_1 (.instr(INSTRUCTION_Next), .rd(rd), .rs1(rs1), .rs2(rs2));
  // Probe on rs1val
  regfile_main RegFile (
    .rs2(rs2), .rd(rd), .Read_Data_1(rs1val), .Read_Data_2(rs2val), .ra(ra), .sp(sp), .t0(t0), .t1(t1),
    .t2(t2), .s0(s0), .s1(s1), .a0(a0), .rs1(rs1), .Write_Data(WBdata), .RegWEn(RegWEn), .clk(CLOCK));
  // Probe on rs2val
  // Probe on BrUn
  // Probe on BrEq
  // Probe on BrLt
  // Probe on ASel
  // Probe on BSel
  // Probe on Imm
  imm_gen imm_gen_1 (.ImmSel(ImmSel), .imm(Imm), .inst(INSTRUCTION_Next));
  // Probe on A
  ASelector aselector_1 (.rs1(rs1val), .PC(PROGRAM_COUNTER_Next), .ASel(ASel), .A(A));
  // Probe on B
  ASelector aselector_2 (.rs1(rs2val), .PC(Imm), .ASel(BSel), .A(B));
  // Probe on ALUSel
  // Probe on A
  // Probe on B
  // Probe on ALURes
  alu Arithmetic_Logic_Unit (.Result(ALURes), .ALUSel(ALUSel), .A(A), .B(B));
  // Probe on ALUSel
  branch_comp branch_comp_1 (.BrEq(BrEq), .BrUn(BrUn), .rs1(rs1val), .BrLt(BrLt), .rs2(rs2val));
  // Probe on MemRW
  // Probe on PROGRAM_COUNTER_Next
  // Probe on ALURes
  // Probe on rs2val
  // Probe on WBSel
  makePCplus4 makepcplus4_1 (.PCval(PROGRAM_COUNTER_Next), .PCplus4(PCplus4));
  // mem_main DMEM: pin names not known; wires that end beside it: ALURes, rs2val, CLOCK, MemRW, MemData, DMEM_p6
  Multiplexer #(.select(2), .width(32), .enable("false")) multiplexer_3 (
    .in0(MemData), .in1(ALURes), .in2(PCplus4), .in3(Imm), .out(WBdata), .sel(WBSel));

  // Other names for the same wires on the sheet: clk = CLOCK; WriteData[31:0] = rs2val; WriteAddr[31:0] = ALURes

  // Notes on the sheet:
  //   IR shows value of second D-latch
  //   Output
  //   IMEM (do **NOT** move this)
  //   Inputs
  //   It is OK to move the PC, RegFile, ALU, MEM, Branch Comp, Imm Gen, and Control Logic to wherever is most convenient for you when constructing your CPU, and to delete this text
  //   Inputs/Outputs for testing. Do **NOT** move these.
endmodule

module getRs (
  input  [31:0] instr,
  output [4:0] rd,
  output [4:0] rs1,
  output [4:0] rs2
);


  assign rd = instr[11:7];
  assign rs1 = instr[19:15];
  assign rs2 = instr[24:20];
endmodule

module ASelector (
  input  [31:0] rs1,
  input  [31:0] PC,
  input  ASel,
  output [31:0] A
);

  Multiplexer #(.width(32), .enable("false")) multiplexer_1 (.in0(rs1), .in1(PC), .out(A), .sel(ASel));
endmodule

module makePCplus4 (
  input  [31:0] PCval,
  output [31:0] PCplus4
);

  Adder #(.width(32)) adder_1 (.a(PCval), .b(32'h4), .out(PCplus4));  // open: cin, cout
endmodule

module makeWriteAddr (
  input  [31:0] instr,
  input  [31:0] writeAddr
);

  wire [6:0] opcode;

  getOP getop_1 (.instr(instr), .opcode(opcode));
endmodule
