// Logisim project imm_gen.circ as structural Verilog: 9 circuits, main circuit imm_gen
module imm_gen (
  input  [31:0] inst,
  input  [2:0] ImmSel,
  output [31:0] imm
);

  wire comparator_1_eq, comparator_2_eq, comparator_3_eq, comparator_4_eq, comparator_5_eq;
  wire [6:0] opcode;
  wire [31:0] I_type, S_type, SB_type, U_type, UJ_type;

  getOP getop_1 (.instr(inst), .opcode(opcode));
  getITypeImm getitypeimm_1 (.instr(inst), .imm(I_type));
  getSTypeImm getstypeimm_1 (.instr(inst), .imm(S_type));
  getSBTypeImm getsbtypeimm_1 (.instr(inst), .imm(SB_type));
  getUTypeImm getutypeimm_1 (.instr(inst), .imm(U_type));
  getUJTypeImm getujtypeimm_1 (.in_1(inst), .out_2(UJ_type));
  Comparator #(.width(3)) comparator_1 (.a(ImmSel), .b(3'b000), .eq(comparator_1_eq));  // open: gt, lt
  Comparator #(.width(3)) comparator_2 (.a(ImmSel), .b(3'b001), .eq(comparator_2_eq));  // open: gt, lt
  Comparator #(.width(3)) comparator_3 (.a(ImmSel), .b(3'b010), .eq(comparator_3_eq));  // open: gt, lt
  Comparator #(.width(3)) comparator_4 (.a(ImmSel), .b(3'b011), .eq(comparator_4_eq));  // open: gt, lt
  Comparator #(.width(3)) comparator_5 (.a(ImmSel), .b(3'b100), .eq(comparator_5_eq));  // open: gt, lt
  assign imm = comparator_1_eq ? I_type : 32'bz;  // Controlled_Buffer I_type
  assign imm = comparator_2_eq ? S_type : 32'bz;  // Controlled_Buffer S_type
  // Probe on imm
  assign imm = comparator_3_eq ? SB_type : 32'bz;  // Controlled_Buffer SB_type
  assign imm = comparator_4_eq ? U_type : 32'bz;  // Controlled_Buffer U_type
  assign imm = comparator_5_eq ? UJ_type : 32'bz;  // Controlled_Buffer UJ_type

  // Notes on the sheet:
  //   INPUTS to your circuit
  //   DON'T CHANGE THE LOCATIONS OF THE INPUTS AND OUTPUTS!
  //   OUTPUT from your circuit
endmodule

module getOP (
  input  [31:0] instr,
  output [6:0] opcode
);


  assign opcode = instr[6:0];
endmodule

module getITypeImm (
  input  [31:0] instr,
  output [31:0] imm
);

  SEXT12TO32 sext12to32_1 (.in_1(instr[31:20]), .out_2(imm));
endmodule

module SEXT12TO32 (
  input  [11:0] in_1,
  output [31:0] out_2
);

  Multiplexer #(.width(21), .enable("false")) multiplexer_1 (
    .in0({21{1'b0}}), .in1({21{1'b1}}), .out(out_2[31:11]), .sel(in_1[11]));

  assign out_2[10:0] = in_1[10:0];
endmodule

module getUTypeImm (
  input  [31:0] instr,
  output [31:0] imm
);

  wire [31:0] sext20to32_1_out_2;

  SEXT20TO32 sext20to32_1 (.in_1(instr[31:12]), .out_2(sext20to32_1_out_2));
  Shifter #(.width(32)) shifter_1 (.in(sext20to32_1_out_2), .\dist (5'b01100), .out(imm));
endmodule

module SEXT20TO32 (
  input  [19:0] in_1,
  output [31:0] out_2
);

  Multiplexer #(.width(13), .enable("false")) multiplexer_1 (
    .in0({13{1'b0}}), .in1({13{1'b1}}), .out(out_2[31:19]), .sel(in_1[19]));

  assign out_2[18:0] = in_1[18:0];
endmodule

module getSTypeImm (
  input  [31:0] instr,
  output [31:0] imm
);

  SEXT12TO32 sext12to32_1 (.in_1({instr[31:25], instr[11:7]}), .out_2(imm));
endmodule

module getSBTypeImm (
  input  [31:0] instr,
  output [31:0] imm
);

  wire [31:0] sext12to32_1_out_2;

  SEXT12TO32 sext12to32_1 (.in_1({instr[31], instr[7], instr[30:25], instr[11:8]}), .out_2(sext12to32_1_out_2));
  Shifter #(.width(32)) shifter_1 (.in(sext12to32_1_out_2), .\dist (5'b00001), .out(imm));
endmodule

module getUJTypeImm (
  input  [31:0] in_1,
  output [31:0] out_2
);

  wire [31:0] sext20to32_1_out_2;

  SEXT20TO32 sext20to32_1 (.in_1({in_1[31], in_1[19:12], in_1[20], in_1[30:21]}), .out_2(sext20to32_1_out_2));
  Shifter #(.width(32)) shifter_1 (.in(sext20to32_1_out_2), .\dist (5'b00001), .out(out_2));
endmodule
