// Logisim project branch_comp.circ as structural Verilog: 1 circuit, main circuit branch_comp
module branch_comp (
  input  [31:0] rs1,
  input  [31:0] rs2,
  input  BrUn,
  output BrEq,
  output BrLt
);

  wire BrLtOri1, BrLtOri2, comparator_1_gt, comparator_2_lt;
  wire [31:0] and_1_out, and_2_out, and_3_out, and_4_out;

  assign and_1_out = rs1 & 32'h80000000;  // AND_Gate and_1, 32 bits wide
  assign and_2_out = rs1 & 32'h7fffffff;  // AND_Gate and_2, 32 bits wide
  // Probe on and_1_out
  assign and_3_out = rs2 & 32'h80000000;  // AND_Gate and_3, 32 bits wide
  assign and_4_out = rs2 & 32'h7fffffff;  // AND_Gate and_4, 32 bits wide
  // Probe on comparator_1_gt
  Comparator #(.width(32)) comparator_1 (.a(and_1_out), .b(and_3_out), .gt(comparator_1_gt));  // open: eq, lt
  Comparator #(.width(32)) comparator_2 (.a(and_2_out), .b(and_4_out), .lt(comparator_2_lt));  // open: gt, eq
  Comparator #(.width(32)) comparator_3 (.a(rs1), .b(rs2), .eq(BrEq));  // open: gt, lt
  Comparator #(.width(32)) comparator_4 (.a(rs1), .b(rs2), .lt(BrLtOri1));  // open: gt, eq
  or or_1 (BrLtOri2, comparator_1_gt, comparator_2_lt);
  Multiplexer #(.enable("false")) multiplexer_1 (.in0(BrLtOri1), .in1(BrLtOri2), .out(BrLt), .sel(BrUn));

  // Notes on the sheet:
  //   INPUTS to your circuit
  //   DON'T CHANGE THE LOCATIONS OF THE INPUTS AND OUTPUTS!
  //   OUTPUT from your circuit
endmodule
