// Logisim project control_logic.circ as structural Verilog: 6 circuits, main circuit control_logic
module control_logic (
  input  [31:0] inst,
  input  BrEq,
  input  BrLt,
  output PCSel,
  output RegWEn,
  output [2:0] ImmSel,
  output BrUn,
  output ASel,
  output BSel,
  output [3:0] ALUSel,
  output MemRW,
  output [1:0] WBSel
);

  wire comparator_1_eq, comparator_2_eq, comparator_3_eq, comparator_4_eq, comparator_5_eq, comparator_6_eq,
       comparator_7_eq, comparator_8_eq, comparator_9_eq, comparator_10_eq, comparator_11_eq,
       comparator_12_eq, comparator_13_eq, comparator_14_eq, comparator_15_eq, comparator_16_eq,
       comparator_17_eq, comparator_18_eq, comparator_19_eq, comparator_20_eq, or_1_out, or_2_out, or_4_out,
       or_5_out, or_6_out, or_7_out;
  wire [6:0] opcode;

  // Probe on 7'b1100111
  // Probe on opcode
  Comparator #(.width(7)) comparator_1 (.a(opcode), .b(7'b0010011), .eq(comparator_1_eq));  // open: gt, lt
  // Probe on 7'b0010011
  Comparator #(.width(7)) comparator_2 (.a(opcode), .b(7'b0000011), .eq(comparator_2_eq));  // open: gt, lt
  // Probe on 7'b0000011
  // Probe on 7'b0100011
  // Probe on 7'b1100011
  // Probe on 7'b0110111
  // Probe on 7'b0010111
  // Probe on 7'b1101111
  // Probe on 7'b1100011
  // Probe on 7'b1101111
  // Probe on 7'b0110011
  Comparator #(.width(7)) comparator_3 (.a(opcode), .b(7'b1100111), .eq(comparator_3_eq));  // open: gt, lt
  assign ImmSel = or_1_out ? 3'b000 : 3'bz;  // Controlled_Buffer I
  or or_1 (or_1_out, comparator_3_eq, comparator_1_eq, comparator_2_eq);
  assign ImmSel = comparator_4_eq ? 3'b001 : 3'bz;  // Controlled_Buffer S
  Comparator #(.width(7)) comparator_4 (.a(opcode), .b(7'b0100011), .eq(comparator_4_eq));  // open: gt, lt
  assign ImmSel = comparator_5_eq ? 3'b010 : 3'bz;  // Controlled_Buffer SB
  Comparator #(.width(7)) comparator_5 (.a(opcode), .b(7'b1100011), .eq(comparator_5_eq));  // open: gt, lt
  Comparator #(.width(7)) comparator_6 (.a(opcode), .b(7'b0110111), .eq(comparator_6_eq));  // open: gt, lt
  Comparator #(.width(7)) comparator_7 (.a(opcode), .b(7'b0010111), .eq(comparator_7_eq));  // open: gt, lt
  assign ImmSel = comparator_8_eq ? 3'b100 : 3'bz;  // Controlled_Buffer UJ
  Comparator #(.width(7)) comparator_8 (.a(opcode), .b(7'b1101111), .eq(comparator_8_eq));  // open: gt, lt
  Comparator #(.width(7)) comparator_9 (.a(opcode), .b(7'b1100011), .eq(comparator_9_eq));  // open: gt, lt
  Comparator #(.width(7)) comparator_10 (.a(opcode), .b(7'b1101111), .eq(comparator_10_eq));  // open: gt, lt
  Comparator #(.width(7)) comparator_11 (.a(opcode), .b(7'b0110011), .eq(comparator_11_eq));  // open: gt, lt
  getOpCode getopcode_1 (.in_1(inst), .out_2(opcode));
  // Probe on opcode
  or or_2 (or_2_out, comparator_6_eq, comparator_7_eq);
  branchCond branchcond_1 (.Instr(inst), .branchEq(BrEq), .branchLt(BrLt), .branchUn(BrUn), .PCSel(PCSel));
  not not_1 (BSel, comparator_11_eq);
  assign ImmSel = or_2_out ? 3'b011 : 3'bz;  // Controlled_Buffer U
  or or_3 (ASel, comparator_9_eq, comparator_10_eq);
  // Probe on ASel
  // Probe on BSel
  // Probe on ImmSel
  // Probe on 7'b0110011
  // Probe on 7'b0010011
  // Probe on 7'b0000011
  // Probe on 7'b1101111
  // Probe on 7'b0110111
  // Probe on 7'b1100111
  // Probe on 7'b0010011
  // Probe on 7'b0110111
  Comparator #(.width(7)) comparator_12 (.a(opcode), .b(7'b0110011), .eq(comparator_12_eq));  // open: gt, lt
  Comparator #(.width(7)) comparator_13 (.a(opcode), .b(7'b0010011), .eq(comparator_13_eq));  // open: gt, lt
  Comparator #(.width(7)) comparator_14 (.a(opcode), .b(7'b0000011), .eq(comparator_14_eq));  // open: gt, lt
  Comparator #(.width(7)) comparator_15 (.a(opcode), .b(7'b1101111), .eq(comparator_15_eq));  // open: gt, lt
  Comparator #(.width(7)) comparator_16 (.a(opcode), .b(7'b0110111), .eq(comparator_16_eq));  // open: gt, lt
  Comparator #(.width(7)) comparator_17 (.a(opcode), .b(7'b1100111), .eq(comparator_17_eq));  // open: gt, lt
  Comparator #(.width(7)) comparator_18 (.a(opcode), .b(7'b0010011), .eq(comparator_18_eq));  // open: gt, lt
  Comparator #(.width(7)) comparator_19 (.a(opcode), .b(7'b0110011), .eq(comparator_19_eq));  // open: gt, lt
  // Probe on 7'b0110011
  Comparator #(.width(7)) comparator_20 (.a(opcode), .b(7'b0110111), .eq(comparator_20_eq));  // open: gt, lt
  or or_4 (or_4_out, comparator_12_eq, comparator_13_eq, comparator_14_eq);
  or or_5 (or_5_out, 1'b0, comparator_15_eq);
  or or_6 (or_6_out, comparator_16_eq, 1'b0);
  or or_7 (or_7_out, comparator_17_eq, 1'b0);
  or or_8 (RegWEn, comparator_18_eq, comparator_19_eq, comparator_20_eq);
  // Probe on ALUSel
  makeALUSel makealusel_1 (.in_1(inst), .out_2(ALUSel));
  assign WBSel = or_4_out ? 2'b00 : 2'bz;  // Controlled_Buffer Selects_ALURes
  assign WBSel = or_5_out ? 2'b01 : 2'bz;  // Controlled_Buffer Selects_PC
  assign WBSel = or_6_out ? 2'b10 : 2'bz;  // Controlled_Buffer Selects_Imm
  assign WBSel = or_7_out ? 2'b11 : 2'bz;  // Controlled_Buffer controlled_buffer_1
  // Probe on RegWEn

  // Notes on the sheet:
  //   INPUTS to your circuit
  //   DON'T CHANGE THE LOCATIONS OF THE INPUTS AND OUTPUTS!
  //   OUTPUT from your circuit
endmodule

module getOpCode (
  input  [31:0] in_1,
  output [6:0] out_2
);

  // Probe on in_1[6:0]

  assign out_2 = in_1[6:0];
endmodule

module getFunc3 (
  input  [31:0] in_1,
  output [2:0] out_2
);


  assign out_2 = in_1[14:12];
endmodule

module getFunc7 (
  input  [31:0] in_1,
  output [6:0] out_2
);


  assign out_2 = in_1[31:25];
endmodule

module makeALUSel (
  input  [31:0] in_1,
  output [3:0] out_2
);

  wire and_1_out, and_2_out, and_3_out, and_4_out, and_5_out, and_6_out, and_7_out, and_8_out, and_9_out,
       and_10_out, and_11_out, and_12_out, and_13_out, and_14_out, and_15_out, and_16_out, and_17_out,
       and_18_out, and_19_out, and_20_out, and_21_out, and_22_out, and_23_out, and_24_out, and_25_out,
       and_26_out, and_27_out, and_28_out, and_29_out, and_30_out, and_31_out, and_32_out, and_33_out,
       and_34_out, and_35_out, comparator_1_eq, comparator_2_eq, comparator_3_eq, comparator_4_eq,
       comparator_5_eq, comparator_6_eq, comparator_7_eq, comparator_8_eq, comparator_9_eq, comparator_10_eq,
       comparator_11_eq, comparator_12_eq, comparator_13_eq, comparator_14_eq, comparator_15_eq,
       comparator_16_eq, comparator_17_eq, comparator_18_eq, comparator_19_eq, comparator_20_eq,
       comparator_21_eq, comparator_22_eq, comparator_23_eq, comparator_24_eq, comparator_25_eq,
       comparator_26_eq, comparator_27_eq, comparator_28_eq, comparator_29_eq, comparator_30_eq,
       comparator_31_eq, comparator_32_eq, comparator_33_eq, comparator_34_eq, comparator_35_eq,
       comparator_36_eq, comparator_37_eq, comparator_38_eq, comparator_39_eq, comparator_40_eq,
       comparator_41_eq, comparator_42_eq, comparator_43_eq, comparator_44_eq, comparator_45_eq,
       comparator_46_eq, comparator_47_eq, comparator_48_eq, comparator_49_eq, comparator_50_eq,
       comparator_51_eq, comparator_52_eq, comparator_53_eq, comparator_54_eq, comparator_55_eq,
       comparator_56_eq, comparator_57_eq, comparator_58_eq, comparator_59_eq, comparator_60_eq,
       comparator_61_eq, comparator_62_eq, comparator_63_eq, comparator_64_eq, comparator_65_eq,
       comparator_66_eq, comparator_67_eq, comparator_68_eq, comparator_69_eq, comparator_70_eq,
       comparator_71_eq, comparator_72_eq, comparator_73_eq, comparator_74_eq, comparator_75_eq,
       comparator_76_eq, comparator_77_eq, comparator_78_eq, comparator_79_eq, comparator_80_eq,
       comparator_81_eq, comparator_82_eq, comparator_83_eq, comparator_84_eq, comparator_85_eq,
       comparator_86_eq, comparator_87_eq, comparator_88_eq, comparator_89_eq, comparator_90_eq, or_1_out;
  wire [2:0] func3;
  wire [6:0] func7, opcode;

  // Probe on opcode
  getOpCode getopcode_1 (.in_1(in_1), .out_2(opcode));
  getFunc3 getfunc3_1 (.in_1(in_1), .out_2(func3));
  getFunc7 getfunc7_1 (.in_1(in_1), .out_2(func7));
  // Probe on opcode
  Comparator #(.width(3)) comparator_1 (.a(func3), .b(3'b110), .eq(comparator_1_eq));  // open: gt, lt
  Comparator #(.width(3)) comparator_2 (.a(func3), .b(3'b111), .eq(comparator_2_eq));  // open: gt, lt
  Comparator #(.width(7)) comparator_3 (.a(func7), .b(7'b0000001), .eq(comparator_3_eq));  // open: gt, lt
  Comparator #(.width(7)) comparator_4 (.a(opcode), .b(7'b0110011), .eq(comparator_4_eq));  // open: gt, lt
  Comparator #(.width(3)) comparator_5 (.a(func3), .b(3'b111), .eq(comparator_5_eq));  // open: gt, lt
  Comparator #(.width(7)) comparator_6 (.a(func7), .b(7'b0000001), .eq(comparator_6_eq));  // open: gt, lt
  Comparator #(.width(7)) comparator_7 (.a(opcode), .b(7'b0110011), .eq(comparator_7_eq));  // open: gt, lt
  Comparator #(.width(7)) comparator_8 (.a(opcode), .b(7'b0110011), .eq(comparator_8_eq));  // open: gt, lt
  Comparator #(.width(3)) comparator_9 (.a(func3), .b(3'b000), .eq(comparator_9_eq));  // open: gt, lt
  Comparator #(.width(7)) comparator_10 (.a(opcode), .b(7'b0010011), .eq(comparator_10_eq));  // open: gt, lt
  Comparator #(.width(3)) comparator_11 (.a(func3), .b(3'b000), .eq(comparator_11_eq));  // open: gt, lt
  Comparator #(.width(3)) comparator_12 (.a(func3), .b(3'b001), .eq(comparator_12_eq));  // open: gt, lt
  Comparator #(.width(7)) comparator_13 (.a(func7), .b(7'b0000001), .eq(comparator_13_eq));  // open: gt, lt
  Comparator #(.width(7)) comparator_14 (.a(opcode), .b(7'b0110011), .eq(comparator_14_eq));  // open: gt, lt
  Comparator #(.width(3)) comparator_15 (.a(func3), .b(3'b000), .eq(comparator_15_eq));  // open: gt, lt
  Comparator #(.width(7)) comparator_16 (.a(func7), .b(7'b0100000), .eq(comparator_16_eq));  // open: gt, lt
  Comparator #(.width(7)) comparator_17 (.a(opcode), .b(7'b0110011), .eq(comparator_17_eq));  // open: gt, lt
  Comparator #(.width(3)) comparator_18 (.a(func3), .b(3'b001), .eq(comparator_18_eq));  // open: gt, lt
  Comparator #(.width(7)) comparator_19 (.a(func7), .b({7{1'b0}}), .eq(comparator_19_eq));  // open: gt, lt
  Comparator #(.width(7)) comparator_20 (.a(opcode), .b(7'b0110011), .eq(comparator_20_eq));  // open: gt, lt
  Comparator #(.width(3)) comparator_21 (.a(func3), .b(3'b001), .eq(comparator_21_eq));  // open: gt, lt
  Comparator #(.width(7)) comparator_22 (.a(func7), .b(7'b0000001), .eq(comparator_22_eq));  // open: gt, lt
  Comparator #(.width(7)) comparator_23 (.a(opcode), .b(7'b0110011), .eq(comparator_23_eq));  // open: gt, lt
  Comparator #(.width(3)) comparator_24 (.a(func3), .b(3'b011), .eq(comparator_24_eq));  // open: gt, lt
  Comparator #(.width(7)) comparator_25 (.a(func7), .b(7'b0000001), .eq(comparator_25_eq));  // open: gt, lt
  Comparator #(.width(7)) comparator_26 (.a(opcode), .b(7'b0110011), .eq(comparator_26_eq));  // open: gt, lt
  Comparator #(.width(3)) comparator_27 (.a(func3), .b(3'b010), .eq(comparator_27_eq));  // open: gt, lt
  Comparator #(.width(7)) comparator_28 (.a(func7), .b({7{1'b0}}), .eq(comparator_28_eq));  // open: gt, lt
  Comparator #(.width(7)) comparator_29 (.a(opcode), .b(7'b0110011), .eq(comparator_29_eq));  // open: gt, lt
  Comparator #(.width(3)) comparator_30 (.a(func3), .b(3'b100), .eq(comparator_30_eq));  // open: gt, lt
  Comparator #(.width(7)) comparator_31 (.a(func7), .b({7{1'b0}}), .eq(comparator_31_eq));  // open: gt, lt
  Comparator #(.width(7)) comparator_32 (.a(opcode), .b(7'b0110011), .eq(comparator_32_eq));  // open: gt, lt
  Comparator #(.width(3)) comparator_33 (.a(func3), .b(3'b101), .eq(comparator_33_eq));  // open: gt, lt
  Comparator #(.width(7)) comparator_34 (.a(func7), .b(7'b0000001), .eq(comparator_34_eq));  // open: gt, lt
  Comparator #(.width(7)) comparator_35 (.a(opcode), .b(7'b0110011), .eq(comparator_35_eq));  // open: gt, lt
  Comparator #(.width(3)) comparator_36 (.a(func3), .b(3'b101), .eq(comparator_36_eq));  // open: gt, lt
  Comparator #(.width(7)) comparator_37 (.a(func7), .b({7{1'b0}}), .eq(comparator_37_eq));  // open: gt, lt
  Comparator #(.width(7)) comparator_38 (.a(opcode), .b(7'b0110011), .eq(comparator_38_eq));  // open: gt, lt
  Comparator #(.width(3)) comparator_39 (.a(func3), .b(3'b101), .eq(comparator_39_eq));  // open: gt, lt
  Comparator #(.width(7)) comparator_40 (.a(func7), .b(7'b0100000), .eq(comparator_40_eq));  // open: gt, lt
  Comparator #(.width(7)) comparator_41 (.a(opcode), .b(7'b0110011), .eq(comparator_41_eq));  // open: gt, lt
  Comparator #(.width(7)) comparator_42 (.a(func7), .b({7{1'b0}}), .eq(comparator_42_eq));  // open: gt, lt
  Comparator #(.width(7)) comparator_43 (.a(opcode), .b(7'b0110011), .eq(comparator_43_eq));  // open: gt, lt
  Comparator #(.width(7)) comparator_44 (.a(func7), .b({7{1'b0}}), .eq(comparator_44_eq));  // open: gt, lt
  and and_1 (and_1_out, comparator_12_eq, comparator_13_eq, comparator_14_eq);
  and and_2 (and_2_out, comparator_15_eq, comparator_16_eq, comparator_17_eq);
  and and_3 (and_3_out, comparator_18_eq, comparator_19_eq, comparator_20_eq);
  and and_4 (and_4_out, comparator_21_eq, comparator_22_eq, comparator_23_eq);
  and and_5 (and_5_out, comparator_24_eq, comparator_25_eq, comparator_26_eq);
  and and_6 (and_6_out, comparator_27_eq, comparator_28_eq, comparator_29_eq);
  and and_7 (and_7_out, comparator_30_eq, comparator_31_eq, comparator_32_eq);
  and and_8 (and_8_out, comparator_33_eq, comparator_34_eq, comparator_35_eq);
  and and_9 (and_9_out, comparator_36_eq, comparator_37_eq, comparator_38_eq);
  and and_10 (and_10_out, comparator_39_eq, comparator_40_eq, comparator_41_eq);
  assign out_2 = and_11_out ? 4'b0010 : 4'bz;  // Controlled_Buffer myOr
  and and_11 (and_11_out, comparator_1_eq, comparator_42_eq, comparator_43_eq);
  assign out_2 = and_12_out ? 4'b1001 : 4'bz;  // Controlled_Buffer myRemu
  and and_12 (and_12_out, comparator_2_eq, comparator_3_eq, comparator_4_eq);
  assign out_2 = and_13_out ? 4'b0001 : 4'bz;  // Controlled_Buffer myAnd
  and and_13 (and_13_out, comparator_5_eq, comparator_6_eq, comparator_7_eq);
  and and_14 (and_14_out, comparator_8_eq, comparator_9_eq, comparator_44_eq);
  and and_15 (and_15_out, comparator_10_eq, comparator_11_eq);
  assign out_2 = and_1_out ? 4'b1010 : 4'bz;  // Controlled_Buffer myMul
  assign out_2 = and_2_out ? 4'b1100 : 4'bz;  // Controlled_Buffer mySub
  assign out_2 = and_3_out ? 4'b0110 : 4'bz;  // Controlled_Buffer mysll
  assign out_2 = and_4_out ? 4'b1110 : 4'bz;  // Controlled_Buffer myMulh
  assign out_2 = and_5_out ? 4'b1011 : 4'bz;  // Controlled_Buffer myMulhu
  assign out_2 = and_6_out ? 4'b0111 : 4'bz;  // Controlled_Buffer mySlt
  assign out_2 = and_7_out ? 4'b0011 : 4'bz;  // Controlled_Buffer myXor
  assign out_2 = and_8_out ? 4'b1000 : 4'bz;  // Controlled_Buffer myDivu
  assign out_2 = and_9_out ? 4'b0100 : 4'bz;  // Controlled_Buffer mySrl
  assign out_2 = and_10_out ? 4'b0101 : 4'bz;  // Controlled_Buffer mySra
  or or_1 (or_1_out, and_14_out, and_15_out);
  assign out_2 = or_1_out ? 4'b0000 : 4'bz;  // Controlled_Buffer add
  Comparator #(.width(3)) comparator_45 (.a(func3), .b(3'b010), .eq(comparator_45_eq));  // open: gt, lt
  Comparator #(.width(3)) comparator_46 (.a(func3), .b(3'b000), .eq(comparator_46_eq));  // open: gt, lt
  Comparator #(.width(7)) comparator_47 (.a(opcode), .b(7'b0010011), .eq(comparator_47_eq));  // open: gt, lt
  Comparator #(.width(3)) comparator_48 (.a(func3), .b(3'b001), .eq(comparator_48_eq));  // open: gt, lt
  Comparator #(.width(7)) comparator_49 (.a(func7), .b({7{1'b0}}), .eq(comparator_49_eq));  // open: gt, lt
  Comparator #(.width(7)) comparator_50 (.a(opcode), .b(7'b0010011), .eq(comparator_50_eq));  // open: gt, lt
  Comparator #(.width(3)) comparator_51 (.a(func3), .b(3'b010), .eq(comparator_51_eq));  // open: gt, lt
  Comparator #(.width(7)) comparator_52 (.a(opcode), .b(7'b0010011), .eq(comparator_52_eq));  // open: gt, lt
  Comparator #(.width(3)) comparator_53 (.a(func3), .b(3'b100), .eq(comparator_53_eq));  // open: gt, lt
  Comparator #(.width(7)) comparator_54 (.a(opcode), .b(7'b0010011), .eq(comparator_54_eq));  // open: gt, lt
  Comparator #(.width(3)) comparator_55 (.a(func3), .b(3'b101), .eq(comparator_55_eq));  // open: gt, lt
  Comparator #(.width(7)) comparator_56 (.a(func7), .b({7{1'b0}}), .eq(comparator_56_eq));  // open: gt, lt
  Comparator #(.width(7)) comparator_57 (.a(opcode), .b(7'b0010011), .eq(comparator_57_eq));  // open: gt, lt
  Comparator #(.width(3)) comparator_58 (.a(func3), .b(3'b101), .eq(comparator_58_eq));  // open: gt, lt
  Comparator #(.width(7)) comparator_59 (.a(func7), .b(7'b0100000), .eq(comparator_59_eq));  // open: gt, lt
  Comparator #(.width(7)) comparator_60 (.a(opcode), .b(7'b0010011), .eq(comparator_60_eq));  // open: gt, lt
  Comparator #(.width(3)) comparator_61 (.a(func3), .b(3'b110), .eq(comparator_61_eq));  // open: gt, lt
  Comparator #(.width(7)) comparator_62 (.a(opcode), .b(7'b0010011), .eq(comparator_62_eq));  // open: gt, lt
  Comparator #(.width(3)) comparator_63 (.a(func3), .b(3'b111), .eq(comparator_63_eq));  // open: gt, lt
  Comparator #(.width(7)) comparator_64 (.a(opcode), .b(7'b0010011), .eq(comparator_64_eq));  // open: gt, lt
  Comparator #(.width(3)) comparator_65 (.a(func3), .b(3'b000), .eq(comparator_65_eq));  // open: gt, lt
  Comparator #(.width(7)) comparator_66 (.a(opcode), .b(7'b0000011), .eq(comparator_66_eq));  // open: gt, lt
  Comparator #(.width(3)) comparator_67 (.a(func3), .b(3'b001), .eq(comparator_67_eq));  // open: gt, lt
  Comparator #(.width(7)) comparator_68 (.a(opcode), .b(7'b0000011), .eq(comparator_68_eq));  // open: gt, lt
  Comparator #(.width(7)) comparator_69 (.a(opcode), .b(7'b0000011), .eq(comparator_69_eq));  // open: gt, lt
  and and_16 (and_16_out, comparator_51_eq, comparator_52_eq);
  and and_17 (and_17_out, comparator_53_eq, comparator_54_eq);
  and and_18 (and_18_out, comparator_55_eq, comparator_56_eq, comparator_57_eq);
  and and_19 (and_19_out, comparator_58_eq, comparator_59_eq, comparator_60_eq);
  and and_20 (and_20_out, comparator_61_eq, comparator_62_eq);
  and and_21 (and_21_out, comparator_63_eq, comparator_64_eq);
  and and_22 (and_22_out, comparator_65_eq, comparator_66_eq);
  and and_23 (and_23_out, comparator_67_eq, comparator_68_eq);
  assign out_2 = and_24_out ? 4'b0000 : 4'bz;  // Controlled_Buffer mylw
  and and_24 (and_24_out, comparator_45_eq, comparator_69_eq);
  assign out_2 = and_25_out ? 4'b0000 : 4'bz;  // Controlled_Buffer myAddi
  and and_25 (and_25_out, comparator_46_eq, comparator_47_eq);
  assign out_2 = and_26_out ? 4'b0110 : 4'bz;  // Controlled_Buffer myslli
  and and_26 (and_26_out, comparator_48_eq, comparator_49_eq, comparator_50_eq);
  assign out_2 = and_16_out ? 4'b0111 : 4'bz;  // Controlled_Buffer myslti
  assign out_2 = and_17_out ? 4'b0011 : 4'bz;  // Controlled_Buffer myXori
  assign out_2 = and_18_out ? 4'b0100 : 4'bz;  // Controlled_Buffer mysrli
  assign out_2 = and_19_out ? 4'b0100 : 4'bz;  // Controlled_Buffer mysrai
  assign out_2 = and_20_out ? 4'b0010 : 4'bz;  // Controlled_Buffer myOri
  assign out_2 = and_21_out ? 4'b0001 : 4'bz;  // Controlled_Buffer myAndi
  assign out_2 = and_22_out ? 4'b0000 : 4'bz;  // Controlled_Buffer mylb
  assign out_2 = and_23_out ? 4'b0000 : 4'bz;  // Controlled_Buffer mylh
  Comparator #(.width(3)) comparator_70 (.a(func3), .b(3'b010), .eq(comparator_70_eq));  // open: gt, lt
  Comparator #(.width(7)) comparator_71 (.a(opcode), .b(7'b0100011), .eq(comparator_71_eq));  // open: gt, lt
  Comparator #(.width(3)) comparator_72 (.a(func3), .b(3'b111), .eq(comparator_72_eq));  // open: gt, lt
  Comparator #(.width(7)) comparator_73 (.a(opcode), .b(7'b0100011), .eq(comparator_73_eq));  // open: gt, lt
  and and_27 (and_27_out, comparator_70_eq, comparator_71_eq);
  and and_28 (and_28_out, comparator_72_eq, comparator_73_eq);
  assign out_2 = and_27_out ? 4'b0000 : 4'bz;  // Controlled_Buffer controlled_buffer_1
  assign out_2 = and_28_out ? 4'b0111 : 4'bz;  // Controlled_Buffer controlled_buffer_2
  Comparator #(.width(3)) comparator_74 (.a(func3), .b(3'b111), .eq(comparator_74_eq));  // open: gt, lt
  Comparator #(.width(3)) comparator_75 (.a(func3), .b(3'b000), .eq(comparator_75_eq));  // open: gt, lt
  Comparator #(.width(7)) comparator_76 (.a(opcode), .b(7'b1100011), .eq(comparator_76_eq));  // open: gt, lt
  Comparator #(.width(3)) comparator_77 (.a(func3), .b(3'b001), .eq(comparator_77_eq));  // open: gt, lt
  Comparator #(.width(7)) comparator_78 (.a(opcode), .b(7'b1100011), .eq(comparator_78_eq));  // open: gt, lt
  Comparator #(.width(3)) comparator_79 (.a(func3), .b(3'b100), .eq(comparator_79_eq));  // open: gt, lt
  Comparator #(.width(7)) comparator_80 (.a(opcode), .b(7'b1100011), .eq(comparator_80_eq));  // open: gt, lt
  Comparator #(.width(3)) comparator_81 (.a(func3), .b(3'b101), .eq(comparator_81_eq));  // open: gt, lt
  Comparator #(.width(7)) comparator_82 (.a(opcode), .b(7'b1100011), .eq(comparator_82_eq));  // open: gt, lt
  Comparator #(.width(3)) comparator_83 (.a(func3), .b(3'b110), .eq(comparator_83_eq));  // open: gt, lt
  Comparator #(.width(7)) comparator_84 (.a(opcode), .b(7'b1100011), .eq(comparator_84_eq));  // open: gt, lt
  Comparator #(.width(7)) comparator_85 (.a(opcode), .b(7'b1100011), .eq(comparator_85_eq));  // open: gt, lt
  and and_29 (and_29_out, comparator_75_eq, comparator_76_eq);
  and and_30 (and_30_out, comparator_77_eq, comparator_78_eq);
  and and_31 (and_31_out, comparator_79_eq, comparator_80_eq);
  and and_32 (and_32_out, comparator_81_eq, comparator_82_eq);
  and and_33 (and_33_out, comparator_83_eq, comparator_84_eq);
  assign out_2 = and_34_out ? 4'b0000 : 4'bz;  // Controlled_Buffer controlled_buffer_3
  and and_34 (and_34_out, comparator_74_eq, comparator_85_eq);
  assign out_2 = and_29_out ? 4'b0000 : 4'bz;  // Controlled_Buffer controlled_buffer_4
  assign out_2 = and_30_out ? 4'b0000 : 4'bz;  // Controlled_Buffer controlled_buffer_5
  assign out_2 = and_31_out ? 4'b0000 : 4'bz;  // Controlled_Buffer controlled_buffer_6
  assign out_2 = and_32_out ? 4'b0000 : 4'bz;  // Controlled_Buffer controlled_buffer_7
  assign out_2 = and_33_out ? 4'b0000 : 4'bz;  // Controlled_Buffer controlled_buffer_8
  Comparator #(.width(3)) comparator_86 (.a(func3), .b(3'b000), .eq(comparator_86_eq));  // open: gt, lt
  Comparator #(.width(7)) comparator_87 (.a(opcode), .b(7'b1100111), .eq(comparator_87_eq));  // open: gt, lt
  Comparator #(.width(7)) comparator_88 (.a(opcode), .b(7'b0010111), .eq(comparator_88_eq));  // open: gt, lt
  Comparator #(.width(7)) comparator_89 (.a(opcode), .b(7'b0110111), .eq(comparator_89_eq));  // open: gt, lt
  Comparator #(.width(7)) comparator_90 (.a(opcode), .b(7'b1101111), .eq(comparator_90_eq));  // open: gt, lt
  assign out_2 = comparator_88_eq ? 4'b0000 : 4'bz;  // Controlled_Buffer controlled_buffer_9
  assign out_2 = comparator_89_eq ? 4'b0000 : 4'bz;  // Controlled_Buffer controlled_buffer_10
  assign out_2 = comparator_90_eq ? 4'b0000 : 4'bz;  // Controlled_Buffer controlled_buffer_11
  assign out_2 = and_35_out ? 4'b0000 : 4'bz;  // Controlled_Buffer controlled_buffer_12
  and and_35 (and_35_out, comparator_86_eq, comparator_87_eq);

  // Other names for the same wires on the sheet: ALUSel[3:0] = out_2

  // Notes on the sheet:
  //   R Type instructions
  //   I type instructions
  //   S type instructions
  //   SB
  //   U
  //   UJ
  //   I
endmodule

module branchCond (
  input  [31:0] Instr,
  input  branchEq,
  input  branchLt,
  output branchUn,
  output PCSel
);

  wire and_1_out, branchConditionSatisfied, comparator_1_eq, comparator_1_lt, comparator_2_eq,
       comparator_3_eq, comparator_4_eq, cond1, cond2, cond3, cond5, cond7;
  wire [2:0] func3;
  wire [6:0] getopcode_1_out_2, getopcode_2_out_2;

  not not_1 (cond1, branchEq);
  not not_2 (cond5, branchLt);
  not not_3 (cond7, branchLt);
  getFunc3 getfunc3_1 (.in_1(Instr), .out_2(func3));
  Comparator #(.width(3)) comparator_1 (.a(func3), .b(3'b110), .eq(comparator_1_eq), .lt(comparator_1_lt));  // open: gt
  Comparator #(.width(3)) comparator_2 (.a(func3), .b(3'b111), .eq(comparator_2_eq));  // open: gt, lt
  // Probe on getopcode_1_out_2
  getOpCode getopcode_1 (.in_1(Instr), .out_2(getopcode_1_out_2));
  getOpCode getopcode_2 (.in_1(Instr), .out_2(getopcode_2_out_2));
  Comparator #(.width(7)) comparator_3 (.a(getopcode_1_out_2), .b(7'b1100011), .eq(comparator_3_eq));  // open: gt, lt
  Comparator #(.width(7)) comparator_4 (.a(getopcode_2_out_2), .b(7'b1100111), .eq(comparator_4_eq));  // open: gt, lt
  or or_1 (branchUn, comparator_1_eq, comparator_2_eq);
  and and_1 (and_1_out, branchConditionSatisfied, comparator_3_eq);
  Multiplexer #(.select(3), .enable("false")) multiplexer_1 (
    .in0(branchEq), .in1(cond1), .in2(cond2), .in3(cond3), .in4(branchLt), .in5(cond5), .in6(branchLt),
    .in7(cond7), .out(branchConditionSatisfied), .sel(func3));
  // Probe on func3
  or or_2 (PCSel, and_1_out, comparator_4_eq);

  // Other names for the same wires on the sheet: beq = branchEq; cond0 = branchEq; blt = branchLt; cond4 = branchLt;
  //   cond6 = branchLt
endmodule
