// Logisim project regfile.circ as structural Verilog: 1 circuit, main circuit main
module main (
  input  [4:0] rs1,
  input  [4:0] rs2,
  input  [4:0] rd,
  input  [31:0] Write_Data,
  input  RegWEn,
  input  clk,
  output [31:0] ra,
  output [31:0] sp,
  output [31:0] t0,
  output [31:0] t1,
  output [31:0] t2,
  output [31:0] s0,
  output [31:0] s1,
  output [31:0] a0,
  output [31:0] Read_Data_1,
  output [31:0] Read_Data_2,
  output [4:0] out_17,
  output [4:0] out_18
);

  wire write_en0, write_en1, write_en2, write_en3, write_en4, write_en5, write_en6, write_en7, write_en8,
       write_en9, write_en10;
  wire [31:0] output0, output3, output4;

  Demultiplexer #(.select(5), .enable("false")) demultiplexer_1 (
    .out0(write_en0), .out1(write_en1), .out2(write_en2), .out3(write_en3), .out4(write_en4),
    .out5(write_en5), .out6(write_en6), .out7(write_en7), .out8(write_en8), .out9(write_en9),
    .out10(write_en10), .in(RegWEn), .sel(rd));  // open: out11, out12, out13, out14, out15, out16, out17, out18, out19, out20, out21, out22, out23, out24, out25, out26, out27, out28, out29, out30, out31
  Register #(.width(32)) register_1 (.D(Write_Data), .en(1'b0), .clk(clk), .Q(output0));  // open: clr
  Register #(.width(32)) register_2 (.D(Write_Data), .en(write_en1), .clk(clk), .Q(ra));  // open: clr
  Register #(.width(32)) register_3 (.D(Write_Data), .en(write_en2), .clk(clk), .Q(sp));  // open: clr
  Register #(.width(32)) register_4 (.D(Write_Data), .en(write_en3), .clk(clk), .Q(output3));  // open: clr
  Register #(.width(32)) register_5 (.D(Write_Data), .en(write_en4), .clk(clk), .Q(output4));  // open: clr
  Register #(.width(32)) register_6 (.D(Write_Data), .en(write_en5), .clk(clk), .Q(t0));  // open: clr
  Register #(.width(32)) register_7 (.D(Write_Data), .en(write_en6), .clk(clk), .Q(t1));  // open: clr
  Register #(.width(32)) register_8 (.D(Write_Data), .en(write_en7), .clk(clk), .Q(t2));  // open: clr
  Register #(.width(32)) register_9 (.D(Write_Data), .en(write_en8), .clk(clk), .Q(s0));  // open: clr
  Register #(.width(32)) register_10 (.D(Write_Data), .en(write_en9), .clk(clk), .Q(s1));  // open: clr
  Register #(.width(32)) register_11 (.D(Write_Data), .en(write_en10), .clk(clk), .Q(a0));  // open: clr
  Multiplexer #(.select(4), .width(32), .enable("false")) multiplexer_1 (
    .in0(output0), .in1(ra), .in2(sp), .in3(output3), .in4(output4), .in5(t0), .in6(t1), .in7(t2), .in8(s0),
    .in9(s1), .in10(a0), .in11({32{1'b0}}), .in12({32{1'b0}}), .in13({32{1'b0}}), .in14({32{1'b0}}),
    .in15({32{1'b0}}), .out(Read_Data_1), .sel(rs1[3:0]));
  Multiplexer #(.select(4), .width(32), .enable("false")) multiplexer_2 (
    .in0(output0), .in1(ra), .in2(sp), .in3(output3), .in4(output4), .in5(t0), .in6(t1), .in7(t2), .in8(s0),
    .in9(s1), .in10(a0), .in11({32{1'b0}}), .in12({32{1'b0}}), .in13({32{1'b0}}), .in14({32{1'b0}}),
    .in15({32{1'b0}}), .out(Read_Data_2), .sel(rs2[3:0]));

  assign out_17 = rs1;
  assign out_18 = rs2;

  // Other names for the same wires on the sheet: output1[31:0] = ra; output2[31:0] = sp; output5[31:0] = t0;
  //   output6[31:0] = t1; output7[31:0] = t2; output8[31:0] = s0; output9[31:0] = s1; output10[31:0] = a0;
  //   read_data1[31:0] = Read_Data_1; read_data2[31:0] = Read_Data_2; read_reg1[4:0] = rs1; read_reg2[4:0] = rs2;
  //   write_en = RegWEn; write_reg[4:0] = rd; x0[31:0] = output0

  // Notes on the sheet:
  //   INPUTS to your circuit
  //   DON'T CHANGE THE LOCATIONS OF THE INPUTS AND OUTPUTS!
  //   These are DEBUG/TEST outputs from your circuit.
  //   OUTPUTS from your circuit
endmodule
